// Logisim project Project.circ as structural Verilog: 13 circuits, main circuit main
// ADDI
module main (
);

  wire aacAll, aacImm, aacOth, ADD, ADDI, AND, ANDI, CF, clk, CMP, controlled_buffer_3_out, Jump, LD, ST,
       xor_1_out, ZF;
  wire [2:0] DR, OpCode, SR1, SR2;
  wire [15:0] address, alu_1_out_5, controlled_buffer_2_out, DRData, FullData, ImmData, multiplexer_1_out,
       pc_1_out_6, PCValue, ram_1_data, SR1Data, SR2Data;

  PC pc_1 (.in_2(PCValue), .ZF(ZF), .CF(CF), .out_6(pc_1_out_6), .in_1(FullData), .in_3(Jump));
  Register #(.width(16)) register_1 (.D(pc_1_out_6), .en(1'b1), .Q(PCValue), .clk(clk));  // open: clr
  ROM #(.addrWidth(16), .dataWidth(16)) rom_1 (.addr(PCValue), .data(FullData));  // open: sel
  Contol_Unit contol_unit_1 (
    .in_4(FullData), .out_6(address), .out_7(SR1), .out_9(SR2), .out_11(DR), .out_5(AND), .out_8(ANDI),
    .out_10(ADD), .out_12(ADDI), .out_17(CMP), .out_18(LD), .out_20(ST), .out_15(aacImm), .out_16(aacOth),
    .out_14(aacAll), .out_19(ImmData), .out_13(OpCode), .out_21(Jump), .out_22(ZF), .out_23(CF), .in_3(clk),
    .in_1(SR1Data), .in_2(SR2Data));
  Clock clock_1 (.out(clk));
  Multiplexer #(.width(16)) multiplexer_1 (
    .in0(SR2Data), .in1(ImmData), .out(multiplexer_1_out), .sel(aacImm));  // open: en
  ALU alu_1 (.in_1(OpCode), .in_2(SR1Data), .out_5(alu_1_out_5), .in_3(multiplexer_1_out));  // open: out_4
  RegisterFile registerfile_1 (
    .SR2(SR2), .SR1(SR1), .clock(clk), .DR(DR), .out_7(SR1Data), .out_6(SR2Data),
    .in_2(controlled_buffer_2_out));
  assign DRData = aacAll ? alu_1_out_5 : 16'bz;  // Controlled_Buffer controlled_buffer_1
  assign controlled_buffer_2_out = xor_1_out ? DRData : 16'bz;  // Controlled_Buffer controlled_buffer_2
  xor xor_1 (xor_1_out, LD, aacAll);
  assign controlled_buffer_3_out = ST ? clk : 1'bz;  // Controlled_Buffer controlled_buffer_3
  RAM #(.addrWidth(16), .dataWidth(16), .bus("separate")) ram_1 (
    .addr(address), .din(SR1Data), .data(ram_1_data), .str(ST), .clk(controlled_buffer_3_out), .ld(LD));  // open: sel, clr
  assign DRData = LD ? ram_1_data : 16'bz;  // Controlled_Buffer controlled_buffer_4

  // Notes on the sheet:
  //   contents of rom_1 (hex, n*v repeats v):
  //   682 299f 4082 7c07 9800 bc01 d003 e404 5603 d005 f004 1603 dc04 ebfb 7603 d005 f403 6e78 e3ee 205
  //   cc04 effc
endmodule

module ALU (
  input  [2:0] in_1,
  input  [15:0] in_2,
  input  [15:0] in_3,
  output out_4,
  output [15:0] out_5
);

  wire decoder_1_out0, decoder_1_out1, decoder_1_out2, decoder_1_out3, or_1_out, or_2_out;
  wire [15:0] adder_1_out_3, and_1_out;

  Decoder #(.select(3)) decoder_1 (
    .out0(decoder_1_out0), .out1(decoder_1_out1), .out2(decoder_1_out2), .out3(decoder_1_out3), .sel(in_1));  // open: out4, out5, out6, out7, en
  or or_1 (or_1_out, decoder_1_out0, decoder_1_out1);
  or or_2 (or_2_out, decoder_1_out2, decoder_1_out3);
  Adder adder_1 (.in_1(in_2), .in_2(in_3), .ADD15(out_4), .out_3(adder_1_out_3));
  assign out_5 = or_2_out ? adder_1_out_3 : 16'bz;  // Controlled_Buffer controlled_buffer_1
  assign out_5 = or_1_out ? and_1_out : 16'bz;  // Controlled_Buffer controlled_buffer_2
  assign and_1_out = in_2 & in_3;  // AND_Gate and_1, 16 bits wide

  // Notes on the sheet:
  //   input 1
  //   input 2
  //   output
endmodule

module Full_Adder (
  input  A,
  input  B,
  input  Carry_in,
  output Carry_out,
  output Result
);

  wire and_1_out, and_2_out, or_1_out;

  or or_1 (or_1_out, B, Carry_in);
  xor xor_1 (Result, A, B, Carry_in);
  and and_1 (and_1_out, ~A, B, Carry_in);  // AND_Gate
  and and_2 (and_2_out, A, or_1_out);
  or or_2 (Carry_out, and_1_out, and_2_out);
endmodule

// ADDER
module Adder (
  input  [15:0] in_1,
  input  [15:0] in_2,
  output [15:0] out_3,
  output ADD15
);

  wire full_adder_1_carry_out, full_adder_2_carry_out, full_adder_3_carry_out, full_adder_4_carry_out,
       full_adder_5_carry_out, full_adder_6_carry_out, full_adder_7_carry_out, full_adder_8_carry_out,
       full_adder_9_carry_out, full_adder_10_carry_out, full_adder_11_carry_out, full_adder_12_carry_out,
       full_adder_13_carry_out, full_adder_14_carry_out, full_adder_15_carry_out;

  Full_Adder full_adder_1 (
    .A(in_1[0]), .B(in_2[0]), .Carry_in(1'b0), .Carry_out(full_adder_1_carry_out), .Result(out_3[0]));
  Full_Adder full_adder_2 (
    .A(in_1[1]), .B(in_2[1]), .Carry_in(full_adder_1_carry_out), .Carry_out(full_adder_2_carry_out),
    .Result(out_3[1]));
  Full_Adder full_adder_3 (
    .A(in_1[2]), .B(in_2[2]), .Carry_in(full_adder_2_carry_out), .Carry_out(full_adder_3_carry_out),
    .Result(out_3[2]));
  Full_Adder full_adder_4 (
    .A(in_1[3]), .B(in_2[3]), .Carry_in(full_adder_3_carry_out), .Carry_out(full_adder_4_carry_out),
    .Result(out_3[3]));
  Full_Adder full_adder_5 (
    .A(in_1[4]), .B(in_2[4]), .Carry_in(full_adder_4_carry_out), .Carry_out(full_adder_5_carry_out),
    .Result(out_3[4]));
  Full_Adder full_adder_6 (
    .A(in_1[5]), .B(in_2[5]), .Carry_in(full_adder_5_carry_out), .Carry_out(full_adder_6_carry_out),
    .Result(out_3[5]));
  Full_Adder full_adder_7 (
    .A(in_1[6]), .B(in_2[6]), .Carry_in(full_adder_6_carry_out), .Carry_out(full_adder_7_carry_out),
    .Result(out_3[6]));
  Full_Adder full_adder_8 (
    .A(in_1[7]), .B(in_2[7]), .Carry_in(full_adder_7_carry_out), .Carry_out(full_adder_8_carry_out),
    .Result(out_3[7]));
  Full_Adder full_adder_9 (
    .A(in_1[8]), .B(in_2[8]), .Carry_in(full_adder_8_carry_out), .Carry_out(full_adder_9_carry_out),
    .Result(out_3[8]));
  Full_Adder full_adder_10 (
    .A(in_1[9]), .B(in_2[9]), .Carry_in(full_adder_9_carry_out), .Carry_out(full_adder_10_carry_out),
    .Result(out_3[9]));
  Full_Adder full_adder_11 (
    .A(in_1[10]), .B(in_2[10]), .Carry_in(full_adder_10_carry_out), .Carry_out(full_adder_11_carry_out),
    .Result(out_3[10]));
  Full_Adder full_adder_12 (
    .A(in_1[11]), .B(in_2[11]), .Carry_in(full_adder_11_carry_out), .Carry_out(full_adder_12_carry_out),
    .Result(out_3[11]));
  Full_Adder full_adder_13 (
    .A(in_1[12]), .B(in_2[12]), .Carry_in(full_adder_12_carry_out), .Carry_out(full_adder_13_carry_out),
    .Result(out_3[12]));
  Full_Adder full_adder_14 (
    .A(in_1[13]), .B(in_2[13]), .Carry_in(full_adder_13_carry_out), .Carry_out(full_adder_14_carry_out),
    .Result(out_3[13]));
  Full_Adder full_adder_15 (
    .A(in_1[14]), .B(in_2[14]), .Carry_in(full_adder_14_carry_out), .Carry_out(full_adder_15_carry_out),
    .Result(out_3[14]));
  Full_Adder full_adder_16 (
    .A(in_1[15]), .B(in_2[15]), .Carry_in(full_adder_15_carry_out), .Carry_out(ADD15), .Result(out_3[15]));

  // Notes on the sheet:
  //   Input 2
  //   Input 1
  //   ADD0
  //   ADD1
  //   ADD2
  //   ADD3
  //   ADD4
  //   ADD5
  //   ADD6
  //   ADD7
  //   ADD8
  //   ADD9
  //   ADD10
  //   ADD11
  //   ADD12
  //   ADD13
  //   ADD14
  //   Output
endmodule

module RegisterFile (
  input  [2:0] SR2,
  input  [15:0] in_2,
  input  [2:0] SR1,
  input  [2:0] DR,
  input  clock,
  output [15:0] out_6,
  output [15:0] out_7
);

  wire and_1_out, and_2_out, and_3_out, and_4_out, and_5_out, and_6_out, and_7_out, and_8_out,
       decoder_1_out0, decoder_1_out1, decoder_1_out2, decoder_1_out3, decoder_1_out4, decoder_1_out5,
       decoder_1_out6, decoder_1_out7, decoder_2_out0, decoder_2_out1, decoder_2_out2, decoder_2_out3,
       decoder_2_out4, decoder_2_out5, decoder_2_out6, decoder_2_out7, decoder_3_out0, decoder_3_out1,
       decoder_3_out2, decoder_3_out3, decoder_3_out4, decoder_3_out5, decoder_3_out6, decoder_3_out7;
  wire [15:0] register_1_q, register_2_q, register_3_q, register_4_q, register_5_q, register_6_q,
       register_7_q, register_8_q;

  Decoder #(.select(3)) decoder_1 (
    .out0(decoder_1_out0), .out1(decoder_1_out1), .out2(decoder_1_out2), .out3(decoder_1_out3),
    .out4(decoder_1_out4), .out5(decoder_1_out5), .out6(decoder_1_out6), .out7(decoder_1_out7), .sel(DR));  // open: en
  and and_1 (and_1_out, decoder_1_out0, 1'b1);
  and and_2 (and_2_out, decoder_1_out1, 1'b1);
  and and_3 (and_3_out, decoder_1_out2, 1'b1);
  and and_4 (and_4_out, decoder_1_out3, 1'b1);
  and and_5 (and_5_out, decoder_1_out4, 1'b1);
  and and_6 (and_6_out, decoder_1_out5, 1'b1);
  and and_7 (and_7_out, decoder_1_out6, 1'b1);
  and and_8 (and_8_out, decoder_1_out7, 1'b1);
  Register #(.width(16)) register_1 (.D(in_2), .en(and_1_out), .Q(register_1_q), .clk(clock));  // open: clr
  Register #(.width(16)) register_2 (.D(in_2), .en(and_2_out), .Q(register_2_q), .clk(clock));  // open: clr
  Register #(.width(16)) register_3 (.D(in_2), .en(and_3_out), .Q(register_3_q), .clk(clock));  // open: clr
  Register #(.width(16)) register_4 (.D(in_2), .en(and_4_out), .Q(register_4_q), .clk(clock));  // open: clr
  Register #(.width(16)) register_5 (.D(in_2), .en(and_5_out), .Q(register_5_q), .clk(clock));  // open: clr
  Register #(.width(16)) register_6 (.D(in_2), .en(and_6_out), .Q(register_6_q), .clk(clock));  // open: clr
  Register #(.width(16)) register_7 (.D(in_2), .en(and_7_out), .Q(register_7_q), .clk(clock));  // open: clr
  Register #(.width(16)) register_8 (.D(in_2), .en(and_8_out), .Q(register_8_q), .clk(clock));  // open: clr
  Decoder #(.select(3)) decoder_2 (
    .out0(decoder_2_out0), .out1(decoder_2_out1), .out2(decoder_2_out2), .out3(decoder_2_out3),
    .out4(decoder_2_out4), .out5(decoder_2_out5), .out6(decoder_2_out6), .out7(decoder_2_out7), .sel(SR1));  // open: en
  assign out_7 = decoder_2_out0 ? register_1_q : 16'bz;  // Controlled_Buffer controlled_buffer_1
  assign out_7 = decoder_2_out1 ? register_2_q : 16'bz;  // Controlled_Buffer controlled_buffer_2
  assign out_7 = decoder_2_out2 ? register_3_q : 16'bz;  // Controlled_Buffer controlled_buffer_3
  assign out_7 = decoder_2_out3 ? register_4_q : 16'bz;  // Controlled_Buffer controlled_buffer_4
  assign out_7 = decoder_2_out4 ? register_5_q : 16'bz;  // Controlled_Buffer controlled_buffer_5
  assign out_7 = decoder_2_out5 ? register_6_q : 16'bz;  // Controlled_Buffer controlled_buffer_6
  assign out_7 = decoder_2_out6 ? register_7_q : 16'bz;  // Controlled_Buffer controlled_buffer_7
  assign out_7 = decoder_2_out7 ? register_8_q : 16'bz;  // Controlled_Buffer controlled_buffer_8
  Decoder #(.select(3)) decoder_3 (
    .out0(decoder_3_out0), .out1(decoder_3_out1), .out2(decoder_3_out2), .out3(decoder_3_out3),
    .out4(decoder_3_out4), .out5(decoder_3_out5), .out6(decoder_3_out6), .out7(decoder_3_out7), .sel(SR2));  // open: en
  assign out_6 = decoder_3_out0 ? register_1_q : 16'bz;  // Controlled_Buffer controlled_buffer_9
  assign out_6 = decoder_3_out1 ? register_2_q : 16'bz;  // Controlled_Buffer controlled_buffer_10
  assign out_6 = decoder_3_out2 ? register_3_q : 16'bz;  // Controlled_Buffer controlled_buffer_11
  assign out_6 = decoder_3_out3 ? register_4_q : 16'bz;  // Controlled_Buffer controlled_buffer_12
  assign out_6 = decoder_3_out4 ? register_5_q : 16'bz;  // Controlled_Buffer controlled_buffer_13
  assign out_6 = decoder_3_out5 ? register_6_q : 16'bz;  // Controlled_Buffer controlled_buffer_14
  assign out_6 = decoder_3_out6 ? register_7_q : 16'bz;  // Controlled_Buffer controlled_buffer_15
  assign out_6 = decoder_3_out7 ? register_8_q : 16'bz;  // Controlled_Buffer controlled_buffer_16

  // Notes on the sheet:
  //   DR Data
  //   load
  //   R0
  //   R1
  //   R2
  //   R3
  //   R4
  //   R5
  //   R6
  //   R7
  //   SR1Data
  //   SR2Data
endmodule

module AndAddControl (
  input  [15:0] in_1,
  input  in_2,
  input  in_3,
  input  in_4,
  input  in_5,
  output [2:0] out_6,
  output [2:0] out_7,
  output [2:0] out_8,
  output [2:0] out_9,
  output out_10,
  output out_11,
  output out_12,
  output [15:0] out_13
);

  wire [6:0] controlled_buffer_1_out;
  wire [15:0] controlled_buffer_3_out;

  assign {out_6, out_7, out_8, controlled_buffer_1_out} = out_10 ? in_1 : 16'bz;  // Controlled_Buffer controlled_buffer_1
  assign out_9 = out_12 ? in_1[2:0] : 3'bz;  // Controlled_Buffer controlled_buffer_2
  or or_1 (out_10, out_12, out_11);
  or or_2 (out_12, in_2, in_4);
  or or_3 (out_11, in_5, in_3);
  assign controlled_buffer_3_out = out_11 ? in_1 : 16'bz;  // Controlled_Buffer controlled_buffer_3
  assign out_13 = {{10{controlled_buffer_3_out[5]}}, controlled_buffer_3_out[5:0]};  // Bit_Extender bit_extender_1
endmodule

module _1_bit_Comparator (
  input  li,
  input  gi,
  input  B,
  input  A,
  output lt_output,
  output gt_output,
  output eq_output
);

  wire and_1_out, and_2_out, and_3_out, and_4_out, and_5_out, nor_1_out, nor_2_out, not_1_out, not_2_out,
       not_3_out, not_4_out;

  not not_1 (not_1_out, gi);
  not not_2 (not_2_out, A);
  not not_3 (not_3_out, B);
  not not_4 (not_4_out, li);
  and and_1 (and_1_out, B, A);
  nor nor_1 (nor_1_out, B, A);
  nor nor_2 (nor_2_out, gi, li);
  or or_1 (lt_output, li, and_2_out);
  and and_2 (and_2_out, B, not_1_out, not_2_out);
  or or_2 (gt_output, gi, and_3_out);
  and and_3 (and_3_out, not_3_out, not_4_out, A);
  and and_4 (and_4_out, and_1_out, nor_2_out);
  or or_3 (eq_output, and_4_out, and_5_out);
  and and_5 (and_5_out, nor_1_out, nor_2_out);
endmodule

module _16_bit_Comparator (
  input  [15:0] in_1,
  input  [15:0] in_2,
  output [2:0] out_3
);

  wire n1_bit_comparator_2_gt_output, n1_bit_comparator_2_lt_output, n1_bit_comparator_3_gt_output,
       n1_bit_comparator_3_lt_output, n1_bit_comparator_4_gt_output, n1_bit_comparator_4_lt_output,
       n1_bit_comparator_5_gt_output, n1_bit_comparator_5_lt_output, n1_bit_comparator_6_gt_output,
       n1_bit_comparator_6_lt_output, n1_bit_comparator_7_gt_output, n1_bit_comparator_7_lt_output,
       n1_bit_comparator_8_gt_output, n1_bit_comparator_8_lt_output, n1_bit_comparator_9_gt_output,
       n1_bit_comparator_9_lt_output, n1_bit_comparator_10_gt_output, n1_bit_comparator_10_lt_output,
       n1_bit_comparator_11_gt_output, n1_bit_comparator_11_lt_output, n1_bit_comparator_12_gt_output,
       n1_bit_comparator_12_lt_output, n1_bit_comparator_13_gt_output, n1_bit_comparator_13_lt_output,
       n1_bit_comparator_14_gt_output, n1_bit_comparator_14_lt_output, n1_bit_comparator_15_gt_output,
       n1_bit_comparator_15_lt_output, n1_bit_comparator_16_gt_output, n1_bit_comparator_16_lt_output;

  _1_bit_Comparator u_1_bit_comparator_1 (
    .lt_output(out_3[1]), .gt_output(out_3[2]), .eq_output(out_3[0]), .li(n1_bit_comparator_2_lt_output),
    .gi(n1_bit_comparator_2_gt_output), .B(in_2[0]), .A(in_1[0]));
  _1_bit_Comparator u_1_bit_comparator_2 (
    .lt_output(n1_bit_comparator_2_lt_output), .gt_output(n1_bit_comparator_2_gt_output),
    .li(n1_bit_comparator_3_lt_output), .gi(n1_bit_comparator_3_gt_output), .B(in_2[1]), .A(in_1[1]));  // open: eq_output
  _1_bit_Comparator u_1_bit_comparator_3 (
    .lt_output(n1_bit_comparator_3_lt_output), .gt_output(n1_bit_comparator_3_gt_output),
    .li(n1_bit_comparator_4_lt_output), .gi(n1_bit_comparator_4_gt_output), .B(in_2[2]), .A(in_1[2]));  // open: eq_output
  _1_bit_Comparator u_1_bit_comparator_4 (
    .lt_output(n1_bit_comparator_4_lt_output), .gt_output(n1_bit_comparator_4_gt_output),
    .li(n1_bit_comparator_5_lt_output), .gi(n1_bit_comparator_5_gt_output), .B(in_2[3]), .A(in_1[3]));  // open: eq_output
  _1_bit_Comparator u_1_bit_comparator_5 (
    .lt_output(n1_bit_comparator_5_lt_output), .gt_output(n1_bit_comparator_5_gt_output),
    .li(n1_bit_comparator_6_lt_output), .gi(n1_bit_comparator_6_gt_output), .B(in_2[4]), .A(in_1[4]));  // open: eq_output
  _1_bit_Comparator u_1_bit_comparator_6 (
    .lt_output(n1_bit_comparator_6_lt_output), .gt_output(n1_bit_comparator_6_gt_output),
    .li(n1_bit_comparator_7_lt_output), .gi(n1_bit_comparator_7_gt_output), .B(in_2[5]), .A(in_1[5]));  // open: eq_output
  _1_bit_Comparator u_1_bit_comparator_7 (
    .lt_output(n1_bit_comparator_7_lt_output), .gt_output(n1_bit_comparator_7_gt_output),
    .li(n1_bit_comparator_8_lt_output), .gi(n1_bit_comparator_8_gt_output), .B(in_2[6]), .A(in_1[6]));  // open: eq_output
  _1_bit_Comparator u_1_bit_comparator_8 (
    .lt_output(n1_bit_comparator_8_lt_output), .gt_output(n1_bit_comparator_8_gt_output),
    .li(n1_bit_comparator_9_lt_output), .gi(n1_bit_comparator_9_gt_output), .B(in_2[7]), .A(in_1[7]));  // open: eq_output
  _1_bit_Comparator u_1_bit_comparator_9 (
    .lt_output(n1_bit_comparator_9_lt_output), .gt_output(n1_bit_comparator_9_gt_output),
    .li(n1_bit_comparator_10_lt_output), .gi(n1_bit_comparator_10_gt_output), .B(in_2[8]), .A(in_1[8]));  // open: eq_output
  _1_bit_Comparator u_1_bit_comparator_10 (
    .lt_output(n1_bit_comparator_10_lt_output), .gt_output(n1_bit_comparator_10_gt_output),
    .li(n1_bit_comparator_11_lt_output), .gi(n1_bit_comparator_11_gt_output), .B(in_2[9]), .A(in_1[9]));  // open: eq_output
  _1_bit_Comparator u_1_bit_comparator_11 (
    .lt_output(n1_bit_comparator_11_lt_output), .gt_output(n1_bit_comparator_11_gt_output),
    .li(n1_bit_comparator_12_lt_output), .gi(n1_bit_comparator_12_gt_output), .B(in_2[10]), .A(in_1[10]));  // open: eq_output
  _1_bit_Comparator u_1_bit_comparator_12 (
    .lt_output(n1_bit_comparator_12_lt_output), .gt_output(n1_bit_comparator_12_gt_output),
    .li(n1_bit_comparator_13_lt_output), .gi(n1_bit_comparator_13_gt_output), .B(in_2[11]), .A(in_1[11]));  // open: eq_output
  _1_bit_Comparator u_1_bit_comparator_13 (
    .lt_output(n1_bit_comparator_13_lt_output), .gt_output(n1_bit_comparator_13_gt_output),
    .li(n1_bit_comparator_14_lt_output), .gi(n1_bit_comparator_14_gt_output), .B(in_2[12]), .A(in_1[12]));  // open: eq_output
  _1_bit_Comparator u_1_bit_comparator_14 (
    .lt_output(n1_bit_comparator_14_lt_output), .gt_output(n1_bit_comparator_14_gt_output),
    .li(n1_bit_comparator_15_lt_output), .gi(n1_bit_comparator_15_gt_output), .B(in_2[13]), .A(in_1[13]));  // open: eq_output
  _1_bit_Comparator u_1_bit_comparator_15 (
    .lt_output(n1_bit_comparator_15_lt_output), .gt_output(n1_bit_comparator_15_gt_output),
    .li(n1_bit_comparator_16_lt_output), .gi(n1_bit_comparator_16_gt_output), .B(in_2[14]), .A(in_1[14]));  // open: eq_output
  _1_bit_Comparator u_1_bit_comparator_16 (
    .lt_output(n1_bit_comparator_16_lt_output), .gt_output(n1_bit_comparator_16_gt_output), .li(1'b0),
    .gi(1'b0), .B(in_2[15]), .A(in_1[15]));  // open: eq_output

  // Notes on the sheet:
  //   Input 2
  //   Input 1
endmodule

module Comparator (
  input  [15:0] in_1,
  input  [15:0] in_2,
  input  [15:0] in_3,
  input  in_4,
  output [2:0] OP1,
  output [2:0] OP2,
  output ZF,
  output CF
);

  wire and_1_out, and_2_out, and_3_out, controlled_buffer_1_out, controlled_buffer_2_out, not_1_out,
       not_2_out, not_3_out, not_4_out, not_5_out, not_6_out, not_7_out, not_8_out, not_9_out, not_10_out;
  wire [2:0] n16_bit_comparator_1_out_3;

  _16_bit_Comparator u_16_bit_comparator_1 (.in_1(in_2), .in_2(in_3), .out_3(n16_bit_comparator_1_out_3));
  not not_1 (not_1_out, n16_bit_comparator_1_out_3[1]);
  and and_1 (and_1_out, n16_bit_comparator_1_out_3[0], not_1_out, not_2_out);
  not not_2 (not_2_out, n16_bit_comparator_1_out_3[2]);
  not not_3 (not_3_out, n16_bit_comparator_1_out_3[0]);
  and and_2 (and_2_out, not_3_out, n16_bit_comparator_1_out_3[1], not_4_out);
  not not_4 (not_4_out, n16_bit_comparator_1_out_3[2]);
  not not_5 (not_5_out, n16_bit_comparator_1_out_3[0]);
  and and_3 (and_3_out, not_5_out, not_6_out, n16_bit_comparator_1_out_3[2]);
  not not_6 (not_6_out, n16_bit_comparator_1_out_3[1]);
  not not_7 (not_7_out, and_1_out);
  not not_8 (not_8_out, and_2_out);
  not not_9 (not_9_out, and_3_out);
  not not_10 (not_10_out, and_3_out);
  assign controlled_buffer_1_out = and_1_out ? and_1_out : 1'bz;  // Controlled_Buffer controlled_buffer_1
  assign controlled_buffer_2_out = and_1_out ? not_7_out : 1'bz;  // Controlled_Buffer controlled_buffer_2
  assign controlled_buffer_1_out = and_2_out ? not_8_out : 1'bz;  // Controlled_Buffer controlled_buffer_3
  assign controlled_buffer_2_out = and_2_out ? and_2_out : 1'bz;  // Controlled_Buffer controlled_buffer_4
  assign controlled_buffer_1_out = and_3_out ? not_9_out : 1'bz;  // Controlled_Buffer controlled_buffer_5
  assign controlled_buffer_2_out = and_3_out ? not_10_out : 1'bz;  // Controlled_Buffer controlled_buffer_6
  Register #(.width(1)) register_1 (.D(controlled_buffer_1_out), .en(1'b1), .Q(ZF), .clk(in_4));  // open: clr
  Register #(.width(1)) register_2 (.D(controlled_buffer_2_out), .en(1'b1), .Q(CF), .clk(in_4));  // open: clr

  assign OP1 = in_1[12:10];
  assign OP2 = in_1[2:0];

  // Notes on the sheet:
  //   FullData
  //   input1
  //   input2
  //   Control
  //   output
endmodule

module Contol_Unit (
  input  [15:0] in_1,
  input  [15:0] in_2,
  input  in_3,
  input  [15:0] in_4,
  output out_5,
  output [15:0] out_6,
  output [2:0] out_7,
  output out_8,
  output [2:0] out_9,
  output out_10,
  output [2:0] out_11,
  output out_12,
  output [2:0] out_13,
  output out_14,
  output out_15,
  output out_16,
  output out_17,
  output out_18,
  output [15:0] out_19,
  output out_20,
  output out_21,
  output out_22,
  output out_23
);

  wire [2:0] andaddcontrol_1_out_6, andaddcontrol_1_out_7, andaddcontrol_1_out_8, andaddcontrol_1_out_9,
       comparator_1_op1, comparator_1_op2, ld_1_out_3, st_1_out_3;
  wire [15:0] andaddcontrol_1_out_13, controlled_buffer_6_out, controlled_buffer_7_out,
       controlled_buffer_12_out, controlled_buffer_13_out, ld_1_out_4, st_1_out_4;

  Decoder #(.select(3)) decoder_1 (
    .out0(out_5), .out1(out_8), .out2(out_10), .out3(out_12), .out4(out_18), .out5(out_20), .out6(out_17),
    .out7(out_21), .sel(in_4[15:13]));  // open: en
  assign out_19 = out_14 ? andaddcontrol_1_out_13 : 16'bz;  // Controlled_Buffer controlled_buffer_1
  AndAddControl andaddcontrol_1 (
    .in_1(in_4), .in_2(out_5), .in_3(out_8), .in_4(out_10), .in_5(out_12), .out_6(andaddcontrol_1_out_6),
    .out_7(andaddcontrol_1_out_7), .out_8(andaddcontrol_1_out_8), .out_9(andaddcontrol_1_out_9),
    .out_10(out_14), .out_11(out_15), .out_12(out_16), .out_13(andaddcontrol_1_out_13));
  assign out_7 = out_14 ? andaddcontrol_1_out_8 : 3'bz;  // Controlled_Buffer controlled_buffer_2
  assign out_9 = out_16 ? andaddcontrol_1_out_9 : 3'bz;  // Controlled_Buffer controlled_buffer_3
  assign out_13 = out_14 ? andaddcontrol_1_out_6 : 3'bz;  // Controlled_Buffer controlled_buffer_4
  assign out_11 = out_14 ? andaddcontrol_1_out_7 : 3'bz;  // Controlled_Buffer controlled_buffer_5
  assign controlled_buffer_6_out = out_18 ? in_4 : 16'bz;  // Controlled_Buffer controlled_buffer_6
  assign controlled_buffer_7_out = out_20 ? in_4 : 16'bz;  // Controlled_Buffer controlled_buffer_7
  assign out_7 = out_17 ? comparator_1_op1 : 3'bz;  // Controlled_Buffer controlled_buffer_8
  LD ld_1 (.in_1(controlled_buffer_6_out), .out_3(ld_1_out_3), .out_4(ld_1_out_4), .in_2(out_18));
  assign out_6 = out_18 ? ld_1_out_4 : 16'bz;  // Controlled_Buffer controlled_buffer_9
  ST st_1 (.in_1(controlled_buffer_7_out), .out_3(st_1_out_3), .out_4(st_1_out_4), .in_2(out_20));
  assign out_6 = out_20 ? st_1_out_4 : 16'bz;  // Controlled_Buffer controlled_buffer_10
  assign out_9 = out_17 ? comparator_1_op2 : 3'bz;  // Controlled_Buffer controlled_buffer_11
  assign controlled_buffer_12_out = out_17 ? in_1 : 16'bz;  // Controlled_Buffer controlled_buffer_12
  assign controlled_buffer_13_out = out_17 ? in_2 : 16'bz;  // Controlled_Buffer controlled_buffer_13
  Comparator comparator_1 (
    .in_1(in_4), .in_2(controlled_buffer_12_out), .in_3(controlled_buffer_13_out), .OP1(comparator_1_op1),
    .OP2(comparator_1_op2), .ZF(out_22), .CF(out_23), .in_4(in_3));
  assign out_11 = out_18 ? ld_1_out_3 : 3'bz;  // Controlled_Buffer controlled_buffer_14
  assign out_7 = out_20 ? st_1_out_3 : 3'bz;  // Controlled_Buffer controlled_buffer_15

  // Other names for the same wires on the sheet: ADD = out_10; ADDI = out_12; Address[15:0] = out_6; AND = out_5;
  //   ANDI = out_8; Clk = in_3; CMP = out_17; DR[2:0] = out_11; FullData[15:0] = in_4; ImmData[15:0] = out_19;
  //   Jump = out_21; LD = out_18; OpCode[2:0] = out_13; SR1[2:0] = out_7; SR1Data[15:0] = in_1; SR2[2:0] = out_9;
  //   SR2Data[15:0] = in_2; ST = out_20

  // Notes on the sheet:
  //   FullData
endmodule

module LD (
  input  [15:0] in_1,
  input  in_2,
  output [2:0] out_3,
  output [15:0] out_4
);

  wire [15:0] controlled_buffer_1_out;

  assign {controlled_buffer_1_out[15:13], out_3, controlled_buffer_1_out[9:0]} = in_2 ? in_1 : 16'bz;  // Controlled_Buffer controlled_buffer_1
  assign out_4 = {{6{1'b0}}, controlled_buffer_1_out[9:0]};  // Bit_Extender bit_extender_1
endmodule

module ST (
  input  [15:0] in_1,
  input  in_2,
  output [2:0] out_3,
  output [15:0] out_4
);

  wire [15:0] controlled_buffer_1_out;

  assign {controlled_buffer_1_out[15:13], out_3, controlled_buffer_1_out[9:0]} = in_2 ? in_1 : 16'bz;  // Controlled_Buffer controlled_buffer_1
  assign out_4 = {{6{1'b0}}, controlled_buffer_1_out[9:0]};  // Bit_Extender bit_extender_1
endmodule

module PC (
  input  [15:0] in_1,
  input  [15:0] in_2,
  input  in_3,
  input  ZF,
  input  CF,
  output [15:0] out_6
);

  wire and_1_out, and_2_out, and_3_out, JA, JAE, JB, JBE, JE, JMP, multiplexer_1_out, multiplexer_2_out,
       multiplexer_3_out, multiplexer_4_out, multiplexer_5_out, multiplexer_6_out, not_1_out, not_2_out,
       not_3_out, not_4_out, not_5_out, or_1_out, or_2_out;
  wire [2:0] multiplexer_7_out;
  wire [15:0] bit_extender_1_out, multiplexer_8_out;

  and and_1 (and_1_out, ZF, not_1_out);
  not not_1 (not_1_out, CF);
  not not_2 (not_2_out, ZF);
  and and_2 (and_2_out, not_2_out, not_3_out);
  not not_3 (not_3_out, CF);
  not not_4 (not_4_out, CF);
  not not_5 (not_5_out, ZF);
  and and_3 (and_3_out, not_5_out, CF);
  or or_1 (or_1_out, ZF, CF);
  Multiplexer multiplexer_1 (.in0(1'b0), .in1(JMP), .out(multiplexer_1_out), .sel(JMP));  // open: en
  Multiplexer multiplexer_2 (.in0(1'b0), .in1(and_1_out), .out(multiplexer_2_out), .sel(JE));  // open: en
  Multiplexer multiplexer_3 (.in0(1'b0), .in1(and_2_out), .out(multiplexer_3_out), .sel(JA));  // open: en
  Multiplexer multiplexer_4 (.in0(1'b0), .in1(not_4_out), .out(multiplexer_4_out), .sel(JAE));  // open: en
  Multiplexer multiplexer_5 (.in0(1'b0), .in1(and_3_out), .out(multiplexer_5_out), .sel(JB));  // open: en
  Multiplexer multiplexer_6 (.in0(1'b0), .in1(or_1_out), .out(multiplexer_6_out), .sel(JBE));  // open: en
  Multiplexer #(.width(3)) multiplexer_7 (
    .in0(3'b111), .in1(in_1[12:10]), .out(multiplexer_7_out), .sel(in_3));  // open: en
  Decoder #(.select(3)) decoder_1 (
    .out0(JMP), .out1(JE), .out2(JA), .out3(JAE), .out4(JB), .out5(JBE), .sel(multiplexer_7_out));  // open: out6, out7, en
  Multiplexer #(.width(16)) multiplexer_8 (
    .in0(16'h1), .in1(in_1), .out(multiplexer_8_out), .sel(or_2_out));  // open: en
  or or_2 (or_2_out, multiplexer_1_out, multiplexer_2_out, multiplexer_3_out, multiplexer_4_out, multiplexer_5_out, multiplexer_6_out);
  assign bit_extender_1_out = {{6{multiplexer_8_out[9]}}, multiplexer_8_out[9:0]};  // Bit_Extender bit_extender_1
  Adder adder_1 (.in_1(in_2), .in_2(bit_extender_1_out), .out_3(out_6));  // open: ADD15

  // Other names for the same wires on the sheet: FullData[15:0] = in_1; Jump = in_3; PCValue[15:0] = in_2

  // Notes on the sheet:
  //   JE
  //   JA
  //   JAE
  //   JB
  //   JBE
endmodule
